# Fritzing sketch 555 PWM (saved by Fritzing 0.9.3b)
perfboards: 1

parts:
  U1 = 555 Timer [package="DIP8 [THT]"]
  R1 = Resistor [tolerance=±5% resistance=1k package=THT]
  R2 = Resistor [tolerance=±5% resistance=1k package=THT]
  C2 = Ceramic Capacitor [capacitance=100nF package="100 mil [THT, multilayer]"]
  VCC1 = Battery
  LED1 = LED - 5mm [color="Red (633nm)" package="5 mm [THT]"]  # not connected
  R3 = Resistor [tolerance=±5% resistance=220 package=THT]
  C1 = Ceramic Capacitor [capacitance=100nF package="100 mil [THT, multilayer]"]
  R4 = Rotary Potentiometer (Small) [maximum_resistance=100kΩ package=THT]

nets:
  N1: U1.Ground, C2.1, VCC1.-, C1.1
  N2: U1.Trigger, U1.Threshold, C1.0, R4.leg2
  N3: U1.Output, R3.Pin_1
  N4: U1.Reset, U1.Vcc_Supply_Voltage, VCC1.+
  N5: U1.Control_Voltage, C2.0
  N6: U1.Discharge, R1.Pin_0, R2.Pin_1
  N7: R2.Pin_0, R4.wiper
