# Fritzing sketch 555 high freq (saved by Fritzing 0.9.3b)
perfboards: 1

parts:
  U1 = 555 Timer [package="DIP8 [THT]"]
  R1 = Resistor [tolerance=±5% resistance=1k package=THT]  # not connected
  R2 = Resistor [tolerance=±5% resistance=1k package=THT]  # not connected
  C2 = Ceramic Capacitor [capacitance=100nF package="100 mil [THT, multilayer]"]  # not connected
  VCC1 = Battery  # not connected
  C1 = Ceramic Capacitor [capacitance=100nF package="100 mil [THT, multilayer]"]  # not connected
  R4 = Rotary Potentiometer (Small) [maximum_resistance=100kΩ package=THT]  # not connected
  Q1 = Basic FET N-Channel [package="TO220 [THT]"]
  Q2 = Basic FET N-Channel [package="TO220 [THT]"]  # not connected
  Q3 = MOSFET-NCHANNEL [part_number=n-ch package=to-92]
  Q4 = MOSFET-NCHANNEL [part_number=p-ch package=to-92]

nets:
  N1: U1.Output, Q3.S, Q4.S
  N2: Q1.source, Q3.G
  N3: Q3.D, Q4.G
