# Fritzing sketch fire_fists (saved by Fritzing 0.9.3b)
circuit board: 10.5222cm x 6.87126cm
breadboards: 1

parts:
  Part1 = Arduino Pro Mini v13
  optoisolator = Optocoupler [package=THT]
  L1 = Solenoid
  arc_lighter = Piezo Speaker
  D1 = Diode [package=diode-1n4001]
  R1 = Resistor [tolerance=±5% resistance=10k package="0603 [SMD]"]
  VCC1 = Battery block 9V
  R2 = Resistor [tolerance=±5% resistance=470 package="0603 [SMD]"]
  S1 = Pushbutton [package=THT]
  R3 = Resistor [tolerance=±5% resistance=330 package="0603 [SMD]"]
  Q1 = Basic FET N-Channel [part_number=IRLZ44NPBF package="TO220 [THT]"]
  Part3 = Triple Axis Accelerometer Breakout - ADXL335

nets:
  VCC: Part1.VCC, Part3.VCC
  GND: Part1.GND, R1.Pin_1, VCC1.-, Q1.source, Part3.GND
  N1: Part1.RAW, L1.pin1, D1.C, S1.leg1
  N2: Part1.A2, Part3.XOUT
  N3: Part1.A1, Part3.YOUT
  N4: Part1.A0, Part3.ZOUT
  N5: Part1.D12/MISO, R3.Pin_0
  N6: optoisolator.Pin_1, R2.Pin_0
  N7: optoisolator.Pin_4, arc_lighter.pin2
  N8: optoisolator.Pin_5, arc_lighter.pin1
  N9: L1.pin2, D1.A, Q1.drain
  N10: R1.Pin_0, R3.Pin_1, Q1.gate
  N11: VCC1.+, S1.leg0

notes:
  filters arc lighter noise
  опционально
  можем добавить R3
