# Fritzing sketch fire_fists_new (saved by Fritzing 0.9.3b)
circuit board: 10.5222cm x 6.87126cm
breadboards: 1

parts:
  Part1 = Arduino Pro Mini v13
  optoisolator = Optocoupler [package=THT]
  L1 = Solenoid
  arc_lighter = Piezo Speaker
  D1 = Diode [package=diode-1n4001]
  R1 = Resistor [tolerance=±5% resistance=10k package="0603 [SMD]"]
  R2 = Resistor [tolerance=±5% resistance=470 package="0603 [SMD]"]
  S1 = Pushbutton [package=THT]
  R3 = Resistor [tolerance=±5% resistance=330 package="0603 [SMD]"]
  Q1 = Basic FET N-Channel [part_number=IRLZ44NPBF package="TO220 [THT]"]
  Part3 = Triple Axis Accelerometer Breakout - ADXL335
  AMS1117_voltage_regulator_(3_3v) = V_REG_MIC2920 [package=sot223]
  liPo = DC Power [voltage=12V]

nets:
  VCC: Part1.VCC, Part3.VCC, AMS1117_voltage_regulator_(3_3v).OUT
  GND: Part1.GND, optoisolator.Pin_2, R1.Pin_1, Q1.source, Part3.GND, AMS1117_voltage_regulator_(3_3v).GND, liPo.V-
  N1: Part1.A2, Part3.ZOUT
  N2: Part1.A1, Part3.YOUT
  N3: Part1.A0, Part3.XOUT
  N4: Part1.D12/MISO, R3.Pin_0
  N5: Part1.D11_PWM/MOSI, R2.Pin_1
  N6: optoisolator.Pin_1, R2.Pin_0
  N7: optoisolator.Pin_4, arc_lighter.pin2
  N8: optoisolator.Pin_5, arc_lighter.pin1
  N9: L1.pin1, D1.C, S1.leg1, AMS1117_voltage_regulator_(3_3v).IN
  N10: L1.pin2, D1.A, Q1.drain
  N11: R1.Pin_0, R3.Pin_1, Q1.gate
  N12: S1.leg0, liPo.V+

notes:
  filters arc lighter noise
  если RAW вход не будет работать, используем регулятор AMS1117
